# Fritzing sketch StopWatchSender (saved by Fritzing 0.9.3b)
breadboards: 1

parts:
  3_3V_-_8MHz = Arduino Pro Mini v13
  Transceiver1 = nRF24L01 [package=module]
  Stop = Pushbutton [package=THT]
  Start0 = Pushbutton [package=THT]
  Start1 = Pushbutton [package=THT]
  Start2 = Pushbutton [package=THT]
  Start3 = Pushbutton [package=THT]
  C1 = Electrolytic Capacitor [capacitance=1µF package="100 mil [THT, electrolytic]"]
  J1 = Piezo Speaker
  V1 = DC Power [voltage=5]

nets:
  GND: 3_3V_-_8MHz.GND, Transceiver1.GND, Stop.leg1, Start0.leg1, Start1.leg1, Start2.leg1, Start3.leg1, C1.-, J1.pin1, V1.V-
  N1: 3_3V_-_8MHz.RAW, V1.V+
  VCC: 3_3V_-_8MHz.VCC, Transceiver1.VCC, C1.+
  N2: 3_3V_-_8MHz.A0, J1.pin2
  N3: 3_3V_-_8MHz.D13/SCK, Transceiver1.SCK
  N4: 3_3V_-_8MHz.D12/MISO, Transceiver1.MISO
  N5: 3_3V_-_8MHz.D11_PWM/MOSI, Transceiver1.MOSI
  N6: 3_3V_-_8MHz.D10_PWM/SS, Transceiver1.CSN
  N7: 3_3V_-_8MHz.D9_PWM, Transceiver1.CE
  N8: 3_3V_-_8MHz.D7, Start3.leg0
  N9: 3_3V_-_8MHz.D6_PWM, Start2.leg0
  N10: 3_3V_-_8MHz.D5_PWM, Start1.leg0
  N11: 3_3V_-_8MHz.D4, Start0.leg0
  N12: 3_3V_-_8MHz.D3_PWM, Stop.leg0
  N13: 3_3V_-_8MHz.D2, Transceiver1.IRQ

notes:
  StopWatchSender

custom parts:
  nRF24L01: nRF24L01 module
